# Fritzing sketch 2 (saved by Fritzing 0.9.5d)
breadboards: 1

parts:
  パーツ1 = Arduino Uno (Rev3)
  LCD1 = LCD screen
  HC-SR04_Sensor_1 = HC-SR04 Ultrasonic Distance Sensor

nets:
  N1: パーツ1.D9_PWM, LCD1.DB4
  N2: パーツ1.D10_PWM/SS, LCD1.DB5
  N3: パーツ1.D11_PWM/MOSI, LCD1.DB6
  N4: パーツ1.D12/MISO, LCD1.DB7
  N5: パーツ1.D2, HC-SR04_Sensor_1.TRIG
  N6: パーツ1.D3_PWM, HC-SR04_Sensor_1.ECHO
  N7: パーツ1.D5_PWM, LCD1.RS
  N8: パーツ1.D6_PWM, LCD1.E
  5V: パーツ1.5V, LCD1.VDD, LCD1.LED+, HC-SR04_Sensor_1.VCC
  GND: パーツ1.GND, LCD1.VSS, LCD1.V0, LCD1.R/W, LCD1.LED-, HC-SR04_Sensor_1.GND
